// Logisim project alu.circ as structural Verilog: 2 circuits, main circuit alu
module alu (
  input  [31:0] A,
  input  [31:0] B,
  input  [3:0] ALUSel,
  output [31:0] Result
);

  wire [0:0] slt7;
  wire [31:0] add0, and1, divu8, mul10, mulh14, mulhu11, or2, remu9, sll6, sra5, srl4, sub12, xor3;

  Adder #(.width(32)) adder_1 (.a(A), .b(B), .out(add0));  // open: cin, cout
  assign and1 = A & B;  // AND_Gate and_1, 32 bits wide
  assign or2 = A | B;  // OR_Gate or_1, 32 bits wide
  assign xor3 = A ^ B;  // XOR_Gate xor_1, 32 bits wide
  Shifter #(.width(32), .shift("lr")) shifter_1 (.in(A), .\dist (B[4:0]), .out(srl4));
  Shifter #(.width(32), .shift("ar")) shifter_2 (.in(A), .\dist (B[4:0]), .out(sra5));
  Shifter #(.width(32)) shifter_3 (.in(A), .\dist (B[4:0]), .out(sll6));
  Comparator #(.width(32)) comparator_1 (.a(A), .b(B), .lt(slt7[0]));  // open: gt, eq
  Divider #(.width(32)) divider_1 (.a(A), .b(B), .out(divu8), .rem(remu9));  // open: upper
  Subtractor #(.width(32)) subtractor_1 (.a(A), .b(B), .out(sub12));  // open: bin, bout
  myMultiplexer mymultiplexer_1 (.A(A), .B(B), .Mul0010(mul10), .Mulh0011(mulhu11), .MUL0014(mulh14));
  Multiplexer #(.select(4), .width(32), .enable("false")) multiplexer_1 (
    .in0(add0), .in1(and1), .in2(or2), .in3(xor3), .in4(srl4), .in5(sra5), .in6(sll6),
    .in7({{31{1'b0}}, slt7[0]}), .in8(divu8), .in9(remu9), .in10(mul10), .in11(mulhu11), .in12(sub12),
    .in13(B), .in14(mulh14), .in15({32{1'b0}}), .out(Result), .sel(ALUSel));

  // Other names for the same wires on the sheet: bsel13[31:0] = B

  // Notes on the sheet:
  //   INPUTS to your circuit
  //   DON'T CHANGE THE LOCATIONS OF THE INPUTS AND OUTPUTS!
  //   OUTPUT from your circuit
endmodule

module myMultiplexer (
  input  [31:0] A,
  input  [31:0] B,
  output [31:0] Mul0010,
  output [31:0] Mulh0011,
  output [31:0] MUL0014
);

  wire [31:0] negator_1_out, negator_2_out, output_01, output_10, output_11;

  Negator #(.width(32)) negator_1 (.in(A), .out(negator_1_out));
  Negator #(.width(32)) negator_2 (.in(B), .out(negator_2_out));
  Multiplier #(.width(32)) multiplier_1 (.a(negator_1_out), .b(negator_2_out), .cout(output_11));  // open: out, cin
  Multiplier #(.width(32)) multiplier_2 (.a(A), .b(B), .out(Mul0010), .cout(Mulh0011));  // open: cin
  Multiplier #(.width(32)) multiplier_3 (.a(A), .b({32{1'b1}}), .out(output_10), .cin(Mulh0011));  // open: cout
  Multiplier #(.width(32)) multiplier_4 (.a(B), .b({32{1'b1}}), .out(output_01), .cin(Mulh0011));  // open: cout
  Multiplexer #(.select(2), .width(32), .enable("false")) multiplexer_1 (
    .in0(Mulh0011), .in1(output_01), .in2(output_10), .in3(output_11), .out(MUL0014), .sel({B[31], A[31]}));

  // Other names for the same wires on the sheet: input1[31:0] = A; input1_sign = A[31]; input2[31:0] = B;
  //   input2_sign = B[31]; output_00[31:0] = Mulh0011
endmodule
