// Logisim project cpu.circ as structural Verilog: 1 circuit, main circuit main
module main (
  input  [31:0] INSTRUCTION,
  input  CLOCK,
  output [31:0] PROGRAM_COUNTER,
  output [31:0] ra,
  output [31:0] sp,
  output [31:0] t0,
  output [31:0] t1,
  output [31:0] t2,
  output [31:0] s0,
  output [31:0] s1,
  output [31:0] a0
);

  wire [31:0] adder_1_out, ALU_result, DMEM_OUTPUT, imm, INSTRUCTION_Pipe, rs1_output, rs2_output, WB_output;

  // control_logic control_logic_1: pin names not known
  Adder #(.width(32)) adder_1 (.a(PROGRAM_COUNTER), .b(32'h4), .out(adder_1_out));  // open: cin, cout
  Register #(.width(32)) PC (.D(adder_1_out), .clk(CLOCK), .Q(PROGRAM_COUNTER));  // open: en, clr
  imm_gen imm_gen_1 (.inst(INSTRUCTION_Pipe), .imm(imm));  // open: ImmSel
  // branch_comp branch_comp_1: pin names not known; wires that end beside it: INSTRUCTION_Pipe
  Register #(.width(32)) register_1 (.D(INSTRUCTION), .clk(CLOCK), .Q(INSTRUCTION_Pipe));  // open: en, clr
  regfile_main RegFile (
    .rs2(INSTRUCTION_Pipe[24:20]), .rd(INSTRUCTION_Pipe[11:7]), .Read_Data_1(rs1_output),
    .Read_Data_2(rs2_output), .ra(ra), .sp(sp), .t0(t0), .t1(t1), .t2(t2), .s0(s0), .s1(s1), .a0(a0),
    .rs1(INSTRUCTION_Pipe[19:15]), .Write_Data(ALU_result), .RegWEn(1'b1), .clk(CLOCK));
  alu Arithmetic_Logic_Unit (.ALUSel(4'b0000), .Result(ALU_result), .A(rs1_output), .B(imm));
  // mem_main DMEM: pin names not known; wires that end beside it: rs2_output, CLOCK, DMEM_OUTPUT
  Multiplexer #(.select(2), .width(32), .enable("false")) multiplexer_1 (
    .in0(ALU_result), .out(WB_output), .sel(2'b00));  // open: in1, in2, in3

  // Other names for the same wires on the sheet: clk = CLOCK

  // Notes on the sheet:
  //   Output
  //   IMEM (do **NOT** move this)
  //   Inputs
  //   It is OK to move the PC, RegFile, ALU, MEM, Branch Comp, Imm Gen, and Control Logic to wherever is most convenient for you when constructing your CPU, and to delete this text
  //   Inputs/Outputs for testing. Do **NOT** move these.
endmodule
